# Fritzing sketch Climares (saved by Fritzing 0.9.5d)
circuit board: 8.46667cm x 5.64444cm

parts:
  DHT1 = DHT11 Humitidy and Temperature Sensor
  U2 = POT [package=pot_mammoth]
  SpeedSensor = FC-03 [chip_label=FC-03]
  YL-83_-_Detection_Board1 = YL-83 Rain Sensor - Detection Board
  M1 = DOIT Esp32 DevKit v1 (30 pins long, 11 pins width) [part_number=ESP32S-PIN30]
  S1 = Hall Sensor [part_number=49e package=TO92]
  R1 = Resistor [tolerance=±5% resistance=220 package=THT]
  YL-83_-_Control_Board1 = YL-83 Rain Sensor - Control Board

nets:
  N1: DHT1.VDD, M1.D23, R1.Pin_0
  N2: DHT1.DATA, R1.Pin_1
  GND: DHT1.GND, U2.S, SpeedSensor.pin_2, M1.GND, S1.GND, YL-83_-_Control_Board1.GND
  N3: U2.A, M1.D34
  VCC: U2.E, SpeedSensor.pin_1, M1.3V3, S1.VCC, YL-83_-_Control_Board1.VCC
  N4: SpeedSensor.pin_3, M1.D22
  N5: YL-83_-_Detection_Board1.POS, YL-83_-_Control_Board1.POS
  N6: YL-83_-_Detection_Board1.NEG, YL-83_-_Control_Board1.NEG
  N7: M1.D35, S1.OUT
  N8: M1.D14, YL-83_-_Control_Board1.DO

custom parts:
  DHT11 Humitidy and Temperature Sensor: DHT11 Humidity and Temperature Sensor
  FC-03: FC-03, LM393 IR Speed Sensor Encoder
  YL-83 Rain Sensor - Detection Board: The YL-83 is a rain sensor that has more resistance when dry and less resistance when wet. The module runs at 5V.
  DOIT Esp32 DevKit v1 (30 pins long, 11 pins width): The DOIT Esp32 DevKit v1 is one of the development board created by DOIT to evaluate the ESP-WROOM-32 module. It is based on the ESP32 microcontroller that boasts Wifi, Bluetooth, Ethernet and Low Power support all in a single chip. (vanepp) made breadboard work, adjusted pin numbering and labels and reduced size of schematic and cleaned up pcb. This chip is 30pins long (2 x15) and 11 pins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
  Hall Sensor: A Hall Sensor
  YL-83 Rain Sensor - Control Board: The YL-83 is a rain sensor that has more resistance when dry and less resistance when wet. The module runs at 5V.
